# Fritzing sketch vent_schematic (saved by Fritzing 1.0.1rc)
breadboards: 1

parts:
  Driver = ESP32S-HiLetgo [part_number=ESP32S-HiLetgo]
  VentDriver_RJ45_1 = RJ45 Jack [package=rj45-8]
  VentDriver_RJ45_2 = RJ45 Jack [package=rj45-8]
  Vent1_RJ45 = RJ45 Jack [package=rj45-8]
  Vent1_Servo = Dagu DGServo 9g (Top view) [part_number=RS001B]
  Vent1_Close_Switch = Toggle Switch [package=THT]
  Vent1_Open_Switch = Toggle Switch [package=THT]
  Vent2_RJ45 = RJ45 Jack [package=rj45-8]
  Vent2_Servo = Dagu DGServo 9g (Top view) [part_number=RS001B]
  Vent2_Open_Switch = Toggle Switch [package=THT]
  Vent2_Close_Switch = Toggle Switch [package=THT]
  M1 = MOSFET-NCHANNEL [package=to220v]
  part = Resistor [tolerance=±2% resistance=150 power=0.25W package="0805 [SMD]"]
  part_2 = Resistor [tolerance=±2% resistance=10k power=0.25W package="0805 [SMD]"]
  part_3 = Resistor [tolerance=±2% resistance=10k power=0.25W package="0805 [SMD]"]
  part_4 = Resistor [tolerance=±2% resistance=10k power=0.25W package="0805 [SMD]"]
  M2 = MOSFET-NCHANNEL [package=to220v]
  part_5 = Resistor [tolerance=±2% resistance=10k power=0.25W package="0805 [SMD]"]
  part_6 = Resistor [tolerance=±2% resistance=10k power=0.25W package="0805 [SMD]"]
  part_7 = Resistor [tolerance=±2% resistance=150 power=0.25W package="0805 [SMD]"]
  part_8 = Resistor [tolerance=±2% resistance=10k power=0.25W package="0805 [SMD]"]

nets:
  N1: Driver.3.3, VentDriver_RJ45_1.1, VentDriver_RJ45_2.1
  N2: Driver.GPIO36, VentDriver_RJ45_2.5, part_5.Pin_0
  N3: Driver.GPIO39, VentDriver_RJ45_2.3, part_6.Pin_0
  N4: Driver.GPIO34, VentDriver_RJ45_1.5, part_4.Pin_0
  N5: Driver.GPIO35, VentDriver_RJ45_1.3, part_3.Pin_0
  N6: Driver.GPIO32, part.Pin_1, part_2.Pin_1
  N7: Driver.GPIO33, part_7.Pin_1, part_8.Pin_1
  N8: Driver.GPIO12, VentDriver_RJ45_1.7, VentDriver_RJ45_2.7
  N9: Driver.GND, M1.S, part_2.Pin_0, part_3.Pin_1, part_4.Pin_1, M2.S, part_5.Pin_1, part_6.Pin_1, part_8.Pin_0
  N10: Driver.VIN, VentDriver_RJ45_1.6, VentDriver_RJ45_1.8, VentDriver_RJ45_2.6, VentDriver_RJ45_2.8
  N11: VentDriver_RJ45_1.2, VentDriver_RJ45_1.4, M1.D
  N12: VentDriver_RJ45_2.2, VentDriver_RJ45_2.4, M2.D
  N13: Vent1_RJ45.1, Vent1_Close_Switch.COM, Vent1_Open_Switch.COM
  N14: Vent1_RJ45.2, Vent1_RJ45.4, Vent1_Servo.gnd
  N15: Vent1_RJ45.3, Vent1_Close_Switch.L2
  N16: Vent1_RJ45.5, Vent1_Open_Switch.L2
  N17: Vent1_RJ45.6, Vent1_RJ45.8, Vent1_Servo.vcc
  N18: Vent1_RJ45.7, Vent1_Servo.pulse
  N19: Vent2_RJ45.1, Vent2_Open_Switch.COM, Vent2_Close_Switch.COM
  N20: Vent2_RJ45.2, Vent2_RJ45.4, Vent2_Servo.gnd
  N21: Vent2_RJ45.3, Vent2_Close_Switch.L2
  N22: Vent2_RJ45.5, Vent2_Open_Switch.L2
  N23: Vent2_RJ45.6, Vent2_RJ45.8, Vent2_Servo.vcc
  N24: Vent2_RJ45.7, Vent2_Servo.pulse
  N25: M1.G, part.Pin_0
  N26: M2.G, part_7.Pin_0

custom parts:
  ESP32S-HiLetgo: HiLetgo ESP-WROOM-32 ESP32 ESP-32S Development Board 2.4GHz Dual-Mode WiFi + Bluetooth Dual Cores Microcontroller The ESP32 integrated with Antenna switches, RF Balun, power amplifiers, low-noise amplifiers, filters, and management modules, and the entire solution occupies the least area of PCB. 2.4 GHz Wi-Fi plus Bluetooth dual-mode chip, with TSMC Ultra-low power consumption 40nm technology,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
